# Fritzing sketch Arduino Architecture (saved by Fritzing 1.0.6)
breadboards: 1

parts:
  Part1 = Arduino Ethernet Shield (Rev3)
  Part2 = Bluetooth HC-05 Macho
  A1 = PIR sensor (non-bendable legs)
  DHT1 = Humidity and Temperature Sensor DHT11
  SG1 = Buzzer 12mm [part_number=COM-07950 package=buzzer-12mm-ns]
  LED1 = LED - 3mm [color="Red (633nm)" current=0.030A package="3 mm [THT]"]
  R1 = Resistor [tolerance=±5% power=0.25W resistance=220 package=THT]

nets:
  N1: Part1.D8, SG1.1
  N2: Part1.ETH_CS, Part2.TXD
  N3: Part1.PWM_D11, Part2.RXD
  GND: Part1.GND, Part2.GND, A1.GND, DHT1.GND_2, SG1.2, LED1.cathode
  N4: Part1.PWM_D3, A1.SIG
  N5: Part1.SDCS, DHT1.GND_1
  N6: Part1.PWM_D6, R1.Pin_1
  5V: Part1.5V, Part2.VCC, A1.VDD, DHT1.Data-signal
  N7: LED1.anode, R1.Pin_0

custom parts:
  PIR sensor (non-bendable legs): Generic PIR sensor
  Humidity and Temperature Sensor DHT11: Digital relative humidity & temperature sensor DHT11
  Buzzer 12mm: Buzzer 12mm Spark Fun Electronics SKU : Comp-Buzzer Through hole This is a small 12mm round speaker that operates around the audible 2kHz range. You can use these speakers to create simple music or user interfaces. This is not a true piezoelectric speaker but behaves similarly. Instead of a piezoelectric crystal that vibrates with an electric current, this tiny speaker uses an electromagnet to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
